// Logisim project partial-store.circ as structural Verilog: 1 circuit, main circuit partial_store
module partial_store (
  input  [31:0] Instruction,
  input  [31:0] MemAddress,
  input  [31:0] DataFromReg,
  input  MemWEn,
  output [3:0] MemWriteMask,
  output [31:0] DataToMem
);

  wire comparator_1_eq, comparator_2_eq, comparator_3_eq, comparator_4_eq, StoreByte, StoreHalf;
  wire [3:0] multiplexer_1_out, multiplexer_4_out, shifter_1_out;
  wire [31:0] Byte_0, Half_0, multiplexer_2_out, multiplexer_3_out, multiplexer_5_out;
  wire [31:8] Byte_1;
  wire [31:16] Byte_2;

  Comparator #(.width(7)) comparator_1 (.a(Instruction[6:0]), .b(7'b0100011), .eq(comparator_1_eq));  // open: gt, lt
  Comparator #(.width(3)) comparator_2 (.a(Instruction[14:12]), .b(3'b000), .eq(comparator_2_eq));  // open: gt, lt
  Comparator #(.width(7)) comparator_3 (.a(Instruction[6:0]), .b(7'b0100011), .eq(comparator_3_eq));  // open: gt, lt
  Comparator #(.width(3)) comparator_4 (.a(Instruction[14:12]), .b(3'b001), .eq(comparator_4_eq));  // open: gt, lt
  and and_1 (StoreByte, comparator_1_eq, comparator_2_eq);
  and and_2 (StoreHalf, comparator_3_eq, comparator_4_eq);
  Multiplexer #(.width(4)) multiplexer_1 (.in0(4'b1111), .in1(4'b0001), .out(multiplexer_1_out), .sel(StoreByte));
  Multiplexer #(.select(2), .width(32)) multiplexer_2 (
    .in0(Byte_0), .in1({Byte_1, {8{1'b0}}}), .in2({Byte_2, {16{1'b0}}}),
    .in3({DataFromReg[7:0], {24{1'b0}}}), .out(multiplexer_2_out), .sel(MemAddress[1:0]));
  assign Byte_0 = {{24{1'b0}}, DataFromReg[7:0]};  // Bit_Extender bit_extender_1
  assign Byte_1 = {{16{1'b0}}, DataFromReg[7:0]};  // Bit_Extender bit_extender_2
  assign Byte_2 = {{8{1'b0}}, DataFromReg[7:0]};  // Bit_Extender bit_extender_3
  Multiplexer #(.width(32)) multiplexer_3 (
    .in0(DataFromReg), .in1(multiplexer_2_out), .out(multiplexer_3_out), .sel(StoreByte));
  Multiplexer #(.width(4)) multiplexer_4 (
    .in0(multiplexer_1_out), .in1(4'b0011), .out(multiplexer_4_out), .sel(StoreHalf));
  assign Half_0 = {{16{1'b0}}, DataFromReg[15:0]};  // Bit_Extender bit_extender_4
  Multiplexer #(.select(2), .width(32)) multiplexer_5 (
    .in0(Half_0), .in2({DataFromReg[15:0], {16{1'b0}}}), .out(multiplexer_5_out), .sel(MemAddress[1:0]));  // open: in1, in3
  Shifter #(.width(4)) shifter_1 (.in(multiplexer_4_out), .\dist (MemAddress[1:0]), .out(shifter_1_out));
  Multiplexer #(.width(32)) multiplexer_6 (
    .in0(multiplexer_3_out), .in1(multiplexer_5_out), .out(DataToMem), .sel(StoreHalf));
  Multiplexer #(.width(4)) multiplexer_7 (.in0(4'b0000), .in1(shifter_1_out), .out(MemWriteMask), .sel(MemWEn));

  // Other names for the same wires on the sheet: Byte_3[31:24] = DataFromReg[7:0]; DataByte[7:0] = DataFromReg[7:0];
  //   DataHalf[15:0] = DataFromReg[15:0]; Half_1[31:16] = DataFromReg[15:0]; opcode[6:0] = Instruction[6:0];
  //   Imm_1[4:0] = Instruction[11:7]; funct3[2:0] = Instruction[14:12]; rs1[4:0] = Instruction[19:15];
  //   rs2[4:0] = Instruction[24:20]; Imm_2[6:0] = Instruction[31:25]; MemLastBits[1:0] = MemAddress[1:0]

  // Notes on the sheet:
  //   INPUTS to your circuit
  //   DON'T CHANGE THE LOCATIONS OF THE INPUTS AND OUTPUTS!
  //   OUTPUT from your circuit
endmodule
