// Logisim project regfile.circ as structural Verilog: 1 circuit, main circuit regfile
module regfile (
  input  [4:0] ReadIndex1,
  input  [4:0] ReadIndex2,
  input  [4:0] WriteIndex,
  input  [31:0] WriteData,
  input  RegWEn,
  input  clk,
  output [31:0] ra,
  output [31:0] sp,
  output [31:0] t0,
  output [31:0] t1,
  output [31:0] t2,
  output [31:0] s0,
  output [31:0] s1,
  output [31:0] a0,
  output [31:0] ReadData1,
  output [31:0] ReadData2
);

  wire WEn1, WEn2, WEn3, WEn4, WEn5, WEn6, WEn7, WEn8, WEn9, WEn10, WEn11, WEn12, WEn13, WEn14, WEn15, WEn16,
       WEn17, WEn18, WEn19, WEn20, WEn21, WEn22, WEn23, WEn24, WEn25, WEn26, WEn27, WEn28, WEn29, WEn30,
       WEn31;
  wire [31:0] a1, a2, a3, a4, a5, a6, a7, s2, s3, s4, s5, s6, s7, s8, s9, s10, s11, t3, t4, t5, t6, x3, x4;

  Register #(.width(32)) register_1 (.D(WriteData), .en(WEn1), .clk(clk), .Q(ra));  // open: clr
  Register #(.width(32)) register_2 (.D(WriteData), .en(WEn2), .clk(clk), .Q(sp));  // open: clr
  Register #(.width(32)) register_3 (.D(WriteData), .en(WEn3), .clk(clk), .Q(x3));  // open: clr
  Register #(.width(32)) register_4 (.D(WriteData), .en(WEn4), .clk(clk), .Q(x4));  // open: clr
  Register #(.width(32)) register_5 (.D(WriteData), .en(WEn5), .clk(clk), .Q(t0));  // open: clr
  Register #(.width(32)) register_6 (.D(WriteData), .en(WEn6), .clk(clk), .Q(t1));  // open: clr
  Register #(.width(32)) register_7 (.D(WriteData), .en(WEn7), .clk(clk), .Q(t2));  // open: clr
  Register #(.width(32)) register_8 (.D(WriteData), .en(WEn8), .clk(clk), .Q(s0));  // open: clr
  Register #(.width(32)) register_9 (.D(WriteData), .en(WEn9), .clk(clk), .Q(s1));  // open: clr
  Register #(.width(32)) register_10 (.D(WriteData), .en(WEn10), .clk(clk), .Q(a0));  // open: clr
  Register #(.width(32)) register_11 (.D(WriteData), .en(WEn11), .clk(clk), .Q(a1));  // open: clr
  Register #(.width(32)) register_12 (.D(WriteData), .en(WEn12), .clk(clk), .Q(a2));  // open: clr
  Register #(.width(32)) register_13 (.D(WriteData), .en(WEn13), .clk(clk), .Q(a3));  // open: clr
  Register #(.width(32)) register_14 (.D(WriteData), .en(WEn14), .clk(clk), .Q(a4));  // open: clr
  Register #(.width(32)) register_15 (.D(WriteData), .en(WEn15), .clk(clk), .Q(a5));  // open: clr
  Multiplexer #(.select(5), .width(32)) multiplexer_1 (
    .in0({32{1'b0}}), .in1(ra), .in2(sp), .in3(x3), .in4(x4), .in5(t0), .in6(t1), .in7(t2), .in8(s0),
    .in9(s1), .in10(a0), .in11(a1), .in12(a2), .in13(a3), .in14(a4), .in15(a5), .in16(a6), .in17(a7),
    .in18(s2), .in19(s3), .in20(s4), .in21(s5), .in22(s6), .in23(s7), .in24(s8), .in25(s9), .in26(s10),
    .in27(s11), .in28(t3), .in29(t4), .in30(t5), .in31(t6), .out(ReadData1), .sel(ReadIndex1));
  Register #(.width(32)) register_16 (.D(WriteData), .en(WEn16), .clk(clk), .Q(a6));  // open: clr
  Register #(.width(32)) register_17 (.D(WriteData), .en(WEn17), .clk(clk), .Q(a7));  // open: clr
  Register #(.width(32)) register_18 (.D(WriteData), .en(WEn18), .clk(clk), .Q(s2));  // open: clr
  Register #(.width(32)) register_19 (.D(WriteData), .en(WEn19), .clk(clk), .Q(s3));  // open: clr
  Register #(.width(32)) register_20 (.D(WriteData), .en(WEn20), .clk(clk), .Q(s4));  // open: clr
  Register #(.width(32)) register_21 (.D(WriteData), .en(WEn21), .clk(clk), .Q(s5));  // open: clr
  Register #(.width(32)) register_22 (.D(WriteData), .en(WEn22), .clk(clk), .Q(s6));  // open: clr
  Register #(.width(32)) register_23 (.D(WriteData), .en(WEn23), .clk(clk), .Q(s7));  // open: clr
  Multiplexer #(.select(5), .width(32)) multiplexer_2 (
    .in0({32{1'b0}}), .in1(ra), .in2(sp), .in3(x3), .in4(x4), .in5(t0), .in6(t1), .in7(t2), .in8(s0),
    .in9(s1), .in10(a0), .in11(a1), .in12(a2), .in13(a3), .in14(a4), .in15(a5), .in16(a6), .in17(a7),
    .in18(s2), .in19(s3), .in20(s4), .in21(s5), .in22(s6), .in23(s7), .in24(s8), .in25(s9), .in26(s10),
    .in27(s11), .in28(t3), .in29(t4), .in30(t5), .in31(t6), .out(ReadData2), .sel(ReadIndex2));
  Register #(.width(32)) register_24 (.D(WriteData), .en(WEn24), .clk(clk), .Q(s8));  // open: clr
  Register #(.width(32)) register_25 (.D(WriteData), .en(WEn25), .clk(clk), .Q(s9));  // open: clr
  Register #(.width(32)) register_26 (.D(WriteData), .en(WEn26), .clk(clk), .Q(s10));  // open: clr
  Register #(.width(32)) register_27 (.D(WriteData), .en(WEn27), .clk(clk), .Q(s11));  // open: clr
  Register #(.width(32)) register_28 (.D(WriteData), .en(WEn28), .clk(clk), .Q(t3));  // open: clr
  Register #(.width(32)) register_29 (.D(WriteData), .en(WEn29), .clk(clk), .Q(t4));  // open: clr
  Register #(.width(32)) register_30 (.D(WriteData), .en(WEn30), .clk(clk), .Q(t5));  // open: clr
  Register #(.width(32)) register_31 (.D(WriteData), .en(WEn31), .clk(clk), .Q(t6));  // open: clr
  Demultiplexer #(.select(5)) demultiplexer_1 (
    .out1(WEn1), .out2(WEn2), .out3(WEn3), .out4(WEn4), .out5(WEn5), .out6(WEn6), .out7(WEn7), .out8(WEn8),
    .out9(WEn9), .out10(WEn10), .out11(WEn11), .out12(WEn12), .out13(WEn13), .out14(WEn14), .out15(WEn15),
    .out16(WEn16), .out17(WEn17), .out18(WEn18), .out19(WEn19), .out20(WEn20), .out21(WEn21), .out22(WEn22),
    .out23(WEn23), .out24(WEn24), .out25(WEn25), .out26(WEn26), .out27(WEn27), .out28(WEn28), .out29(WEn29),
    .out30(WEn30), .out31(WEn31), .in(RegWEn), .sel(WriteIndex));  // open: out0

  // Other names for the same wires on the sheet: x1[31:0] = ra; x2[31:0] = sp; x5[31:0] = t0; x6[31:0] = t1;
  //   x7[31:0] = t2; x8[31:0] = s0; x9[31:0] = s1; x10[31:0] = a0; x11[31:0] = a1; x12[31:0] = a2; x13[31:0] = a3;
  //   x14[31:0] = a4; x15[31:0] = a5; x16[31:0] = a6; x17[31:0] = a7; x18[31:0] = s2; x19[31:0] = s3; x20[31:0] = s4;
  //   x21[31:0] = s5; x22[31:0] = s6; x23[31:0] = s7; x24[31:0] = s8; x25[31:0] = s9; x26[31:0] = s10;
  //   x27[31:0] = s11; x28[31:0] = t3; x29[31:0] = t4; x30[31:0] = t5; x31[31:0] = t6

  // Notes on the sheet:
  //   INPUTS to your circuit
  //   DON'T CHANGE THE LOCATIONS OF THE INPUTS AND OUTPUTS!
  //   These are DEBUG/TEST outputs from your circuit.
  //   OUTPUTS from your circuit
endmodule
